// Logisim project 1.circ as structural Verilog: 1 circuit, main circuit main
module main (
  input  x3,
  input  x0,
  input  x2,
  input  x1,
  output out_5
);

  wire and_1_out, and_2_out, and_3_out, not_1_out, not_2_out;

  not not_1 (not_1_out, x0);
  not not_2 (not_2_out, x1);
  and and_1 (and_1_out, x3, not_1_out);
  and and_2 (and_2_out, x0, x2, not_2_out);
  and and_3 (and_3_out, x1, x3);
  or or_1 (out_5, and_1_out, and_2_out, and_3_out);
endmodule
