// Logisim project 22.circ as structural Verilog: 1 circuit, main circuit main
module main (
  input  x0,
  input  x1,
  input  x2,
  output f0,
  output f1,
  output f2,
  output f3,
  output f4,
  output f5,
  output f6,
  output f7
);

  wire not_1_out, not_2_out, not_3_out;

  not not_1 (not_1_out, x0);
  not not_2 (not_2_out, x1);
  not not_3 (not_3_out, x2);
  and and_1 (f0, not_1_out, not_2_out, not_3_out);
  and and_2 (f1, not_2_out, not_3_out, x0);
  and and_3 (f2, x1, not_1_out, not_3_out);
  and and_4 (f3, x1, x0, not_3_out);
  and and_5 (f4, not_1_out, not_2_out, x2);
  and and_6 (f5, x0, not_2_out, x2);
  and and_7 (f6, not_1_out, x1, x2);
  and and_8 (f7, x0, x1, x2);
endmodule
